# Fritzing sketch ESP8266_SensorBoard (saved by Fritzing 0.9.1b)
circuit board: 5cm x 5cm
breadboards: 1

parts:
  DHT22 = DHT22 Humidity and Temperature Sensor
  LDR = Photocell (LDR) [package=THT]
  IC1 = Voltage Regulator LM1117 [package=sot223]
  VCC_3_3/5 = screw terminal, 2 pins
  R1 = Resistor [tolerance=±5% resistance=4.7k package=THT]
  3_3V_5V = male pin header, 3 pins [form="♂ (male)"]
  ESP-07/12 = ESP8266-12 WiFi Module [part_number=ESP8266]
  R2 = Resistor [tolerance=±5% resistance=100k package=THT]
  S1 = Pushbutton [package="[THT]"]
  RS232 = male pin header, 3 pins [form="♂ (male)"]
  S2 = Pushbutton [package="[THT]"]
  R4 = Resistor [tolerance=±5% resistance=4.7k package=THT]
  R5 = Resistor [tolerance=±5% resistance=4.7k package=THT]
  R6 = Resistor [tolerance=±5% resistance=4.7k package=THT]
  D1 = Zener Diode [part_number=1N4732A breakdown_voltage=3.6V package="300 mil [THT]"]
  R7 = Resistor [tolerance=±5% resistance=220k package=THT]

nets:
  N1: DHT22.VDD, R1.Pin_0, ESP-07/12.GPIO_14
  N2: DHT22.DATA, R1.Pin_1, ESP-07/12.GPIO_12
  GND: DHT22.GND, IC1.ADJ, VCC_3_3/5.pin2, ESP-07/12.GND, ESP-07/12.GPIO_15, R2.Pin_0, S1.Pin_3, S1.Pin_4, RS232.pin3, S2.Pin_3, S2.Pin_4
  N3: LDR.pin_0, 3_3V_5V.pin1, ESP-07/12.VCC, ESP-07/12.CH_PD, R4.Pin_0, R5.Pin_0, R6.Pin_0, D1.cathode
  N4: LDR.pin_1, R7.Pin_0
  N5: IC1.OUT, D1.anode
  N6: IC1.IN, 3_3V_5V.pin3
  N7: VCC_3_3/5.pin1, 3_3V_5V.pin2
  N8: ESP-07/12.RXD, RS232.pin1
  N9: ESP-07/12.GPIO_0, S1.Pin_1, S1.Pin_2, R5.Pin_1
  N10: ESP-07/12.GPIO_16, ESP-07/12.RESET, S2.Pin_1, S2.Pin_2, R6.Pin_1
  N11: ESP-07/12.GPIO_2, R4.Pin_1
  N12: ESP-07/12.TXD, RS232.pin2
  N13: ESP-07/12.ADC, R2.Pin_1, R7.Pin_1

notes:
  -  +
  TX
  GND
  RX
  bluewalk.net
  Flash
  Reset

custom parts:
  ESP8266-12 WiFi Module: Generic WiFi Module based on the ESP8266 with onboard PCB antenna and UART communications
